# Fritzing sketch sonar1 (saved by Fritzing 0.9.10b)
breadboards: 1

parts:
  부품1 = Arduino Mega 2560 (Rev3)
  HC-SR04_Sensor_1 = HC-SR04 Ultrasonic Distance Sensor

nets:
  5V: 부품1.5V, HC-SR04_Sensor_1.VCC
  VIN: 부품1.VIN, HC-SR04_Sensor_1.GND
  N1: 부품1.D5_PWM, HC-SR04_Sensor_1.TRIG
  N2: 부품1.D6_PWM, HC-SR04_Sensor_1.ECHO
