# Fritzing sketch sonar3_motor (saved by Fritzing 0.9.10b)
breadboards: 1

parts:
  S1 = H-Bridge with L298N
  부품1 = Arduino Mega 2560 (Rev3)
  VCC1 = Battery
  HC-SR04_Sensor_2 = HC-SR04 Ultrasonic Distance Sensor
  HC-SR04_Sensor_3 = HC-SR04 Ultrasonic Distance Sensor
  HC-SR04_Sensor_4 = HC-SR04 Ultrasonic Distance Sensor

nets:
  N1: S1.12V, VCC1.+
  GND: S1.GND, 부품1.GND, VCC1.-
  VCC: S1.5V, 부품1.5V, HC-SR04_Sensor_2.VCC, HC-SR04_Sensor_3.VCC, HC-SR04_Sensor_4.VCC
  N2: S1.ENA, 부품1.D8_PWM
  N3: S1.IN1, 부품1.D9_PWM
  N4: S1.IN2, 부품1.D10_PWM
  GND_2: 부품1.VIN, HC-SR04_Sensor_2.GND, HC-SR04_Sensor_3.GND, HC-SR04_Sensor_4.GND
  N5: 부품1.D2_PWM, HC-SR04_Sensor_3.TRIG
  N6: 부품1.D3_PWM, HC-SR04_Sensor_3.ECHO
  N7: 부품1.D4_PWM, HC-SR04_Sensor_4.TRIG
  N8: 부품1.D5_PWM, HC-SR04_Sensor_4.ECHO
  N9: 부품1.D6_PWM, HC-SR04_Sensor_2.TRIG
  N10: 부품1.D7_PWM, HC-SR04_Sensor_2.ECHO

custom parts:
  H-Bridge with L298N: h-bridge
